// Logisim project yamcufs.circ as structural Verilog: 1 circuit, main circuit main
module main (
  input  in_1,
  input  [3:0] in_2
);

  wire alu_main_1_p4, and_1_out, BRANCH, clock_1_out, clock_2_out, clock_3_out, decoder_1_out0,
       decoder_1_out1, decoder_1_out2, decoder_1_out3, decoder_1_out4, decoder_1_out5, decoder_1_out6,
       decoder_1_out7, decoder_1_out8, decoder_1_out9, decoder_1_out10, decoder_1_out11, decoder_1_out12,
       decoder_1_out13, decoder_1_out14, JAL_TO_REG, LOAD_IMM, MEM_READ, MEM_TO_REG, MEM_WRITE, MUX_IMM,
       or_1_out, or_2_out, PC_ADRESS;
  wire [3:0] ALU_OP;
  wire [15:0] adder_1_out, alu_main_1_p5, bit_extender_1_out, bit_extender_2_out, JR_ADRESS,
       multiplexer_1_out, multiplexer_2_out, multiplexer_4_out, multiplexer_5_out, PC_IMM,
       pc_main_1_adress_out, ram_1_dout, reg_file_1_b, rom_1_data;

  Multiplexer #(.width(16)) multiplexer_1 (
    .in0(multiplexer_4_out), .in1(adder_1_out), .out(multiplexer_1_out), .sel(or_1_out));
  PC_Main pc_main_1 (
    .JR_Enable(JAL_TO_REG), .CLK(clock_1_out), .JR_Adress(JR_ADRESS), .PC_Src(or_1_out), .Reset(in_1),
    .Adress_Write(multiplexer_1_out), .Adress_Out(pc_main_1_adress_out));  // open: Halt
  Clock clock_1 (.out(clock_1_out));
  Decoder #(.select(4)) decoder_1 (
    .out0(decoder_1_out0), .out1(decoder_1_out1), .out2(decoder_1_out2), .out3(decoder_1_out3),
    .out4(decoder_1_out4), .out5(decoder_1_out5), .out6(decoder_1_out6), .out7(decoder_1_out7),
    .out8(decoder_1_out8), .out9(decoder_1_out9), .out10(decoder_1_out10), .out11(decoder_1_out11),
    .out12(decoder_1_out12), .out13(decoder_1_out13), .out14(decoder_1_out14), .out15(JAL_TO_REG),
    .sel(rom_1_data[15:12]), .en(1'b1));
  ROM #(.addrWidth(16), .dataWidth(16)) rom_1 (.addr(pc_main_1_adress_out), .data(rom_1_data));
  Adder #(.width(16)) adder_1 (.a(PC_IMM), .b(pc_main_1_adress_out), .out(adder_1_out));  // open: cin, cout
  or or_1 (or_1_out, PC_ADRESS, and_1_out);
  and and_1 (and_1_out, BRANCH, alu_main_1_p4);
  or or_2 (or_2_out, decoder_1_out0, decoder_1_out1, decoder_1_out2, decoder_1_out3, decoder_1_out4, decoder_1_out5, decoder_1_out6, decoder_1_out7, decoder_1_out8, decoder_1_out9, decoder_1_out10, decoder_1_out11, JAL_TO_REG);
  buf or_3 (MEM_READ, decoder_1_out11);  // OR_Gate
  buf or_4 (MEM_WRITE, decoder_1_out12);  // OR_Gate
  buf or_5 (PC_ADRESS, decoder_1_out14);  // OR_Gate
  buf or_6 (MUX_IMM, decoder_1_out14);  // OR_Gate
  or or_7 (LOAD_IMM, decoder_1_out9, decoder_1_out11, decoder_1_out12, JAL_TO_REG);
  buf or_8 (MEM_TO_REG, decoder_1_out11);  // OR_Gate
  or or_9 (ALU_OP[0], decoder_1_out1, decoder_1_out3, decoder_1_out5, decoder_1_out7, decoder_1_out13);
  or or_10 (ALU_OP[1], decoder_1_out2, decoder_1_out3, decoder_1_out6, decoder_1_out7, decoder_1_out10);
  or or_11 (ALU_OP[2], decoder_1_out4, decoder_1_out5, decoder_1_out6, decoder_1_out7);
  buf or_12 (ALU_OP[3], decoder_1_out8);  // OR_Gate
  buf or_13 (BRANCH, decoder_1_out13);  // OR_Gate
  Multiplexer #(.width(16)) multiplexer_2 (
    .in0(multiplexer_4_out), .in1(pc_main_1_adress_out), .out(multiplexer_2_out), .sel(JAL_TO_REG));
  Clock clock_2 (.out(clock_2_out));
  assign bit_extender_1_out = {{12{rom_1_data[11]}}, rom_1_data[11:8]};  // Bit_Extender bit_extender_1
  assign bit_extender_2_out = {{4{rom_1_data[11]}}, rom_1_data[11:0]};  // Bit_Extender bit_extender_2
  REG_File reg_file_1 (
    .Reset(in_1), .Reg_Sel_A(rom_1_data[7:4]), .Reg_Sel_B(rom_1_data[3:0]), .Write_Enable(or_2_out),
    .Write_Reg(rom_1_data[11:8]), .Write_Data(multiplexer_2_out), .CLK(clock_2_out), .A(JR_ADRESS),
    .B(reg_file_1_b));
  Multiplexer #(.width(16)) multiplexer_3 (
    .in0(bit_extender_1_out), .in1(bit_extender_2_out), .out(PC_IMM), .sel(MUX_IMM));
  Multiplexer #(.width(16)) multiplexer_4 (
    .in0(alu_main_1_p5), .in1(ram_1_dout), .out(multiplexer_4_out), .sel(MEM_TO_REG));
  Multiplexer #(.width(16)) multiplexer_5 (.in0(reg_file_1_b), .in1(PC_IMM), .out(multiplexer_5_out), .sel(LOAD_IMM));
  // ALU_Main alu_main_1: pin names not known; wires that end beside it: JR_ADRESS, multiplexer_5_out, ALU_OP, alu_main_1_p4, alu_main_1_p5
  RAM #(.addrWidth(16), .dataWidth(16)) ram_1 (
    .addr(alu_main_1_p5), .we(MEM_WRITE), .oe(MEM_READ), .clk(clock_3_out), .din(reg_file_1_b),
    .dout(ram_1_dout));
  Clock clock_3 (.out(clock_3_out));

  // Other names for the same wires on the sheet: JR_ENABLE = JAL_TO_REG; Reset = in_1

  // Notes on the sheet:
  //   contents of rom_1 (hex, n*v repeats v):
  //   f000
  //   MEM_READ
  //   MEM_WRITE
  //   PC_ADRESS
  //   MUX_2
  //   MUX_3
  //   ALU_B0
  //   ALU_B1
  //   ALU_B2
  //   ALU_B3
  //   BRANCH
  //   REG_WRITE_ENABLE
  //   MUX_1 - SELECT_IMM
  //   M2
endmodule
